// Logisim project 7_segment_display.circ as structural Verilog: 9 circuits, main circuit main
module main (
  input  SW_3,
  input  SW_2,
  input  SW_1,
  input  SW_0
);

  wire segment_0_1_s_0, segment_1_1_s_1, segment_2_1_s_2, segment_3_1_s_3, segment_4_1_s_4, segment_5_1_s_5,
       segment_6_1_s_6;

  segment_0 segment_0_1 (.c_3(SW_3), .c_2(SW_2), .c_1(SW_1), .c_0(SW_0), .s_0(segment_0_1_s_0));
  _7_Segment_Display u_7_segment_display_1 (
    .g(segment_6_1_s_6), .f(segment_5_1_s_5), .a(segment_0_1_s_0), .b(segment_1_1_s_1), .e(segment_4_1_s_4),
    .d(segment_3_1_s_3), .c(segment_2_1_s_2));  // open: dp
  segment_1 segment_1_1 (.c_3(SW_3), .c_2(SW_2), .c_1(SW_1), .c_0(SW_0), .s_1(segment_1_1_s_1));
  segment_2 segment_2_1 (.c_3(SW_3), .c_2(SW_2), .c_1(SW_1), .c_0(SW_0), .s_2(segment_2_1_s_2));
  segment_3 segment_3_1 (.c_3(SW_3), .c_2(SW_2), .c_1(SW_1), .c_0(SW_0), .s_3(segment_3_1_s_3));
  segment_4 segment_4_1 (.c_3(SW_3), .c_2(SW_2), .c_1(SW_1), .c_0(SW_0), .s_4(segment_4_1_s_4));
  segment_5 segment_5_1 (.c_3(SW_3), .c_2(SW_2), .c_1(SW_1), .c_0(SW_0), .s_5(segment_5_1_s_5));
  segment_6 segment_6_1 (.c_3(SW_3), .c_2(SW_2), .c_1(SW_1), .c_0(SW_0), .s_6(segment_6_1_s_6));
endmodule

module segment_0 (
  input  c_3,
  input  c_2,
  input  c_1,
  input  c_0,
  output s_0
);

  wire and_1_out, and_2_out, and_3_out, and_4_out, and_5_out, and_6_out, not_1_out, not_2_out, not_3_out,
       not_4_out, not_5_out, not_6_out, not_7_out;

  not not_1 (not_1_out, c_2);
  and and_1 (and_1_out, c_3, not_1_out, not_2_out);
  not not_2 (not_2_out, c_1);
  not not_3 (not_3_out, c_3);
  and and_2 (and_2_out, not_3_out, c_2, c_0);
  and and_3 (and_3_out, c_3, not_4_out);
  not not_4 (not_4_out, c_0);
  and and_4 (and_4_out, c_2, c_1);
  not not_5 (not_5_out, c_3);
  and and_5 (and_5_out, not_5_out, c_1);
  not not_6 (not_6_out, c_2);
  and and_6 (and_6_out, not_6_out, not_7_out);
  not not_7 (not_7_out, c_0);
  or or_1 (s_0, and_1_out, and_2_out, and_3_out, and_4_out, and_5_out, and_6_out);
endmodule

module segment_1 (
  input  c_3,
  input  c_2,
  input  c_1,
  input  c_0,
  output s_1
);

  wire and_1_out, and_2_out, and_3_out, and_4_out, and_5_out, not_1_out, not_2_out, not_3_out, not_4_out,
       not_5_out, not_6_out, not_7_out, not_8_out, not_9_out;

  not not_1 (not_1_out, c_3);
  and and_1 (and_1_out, not_1_out, not_2_out);
  not not_2 (not_2_out, c_2);
  not not_3 (not_3_out, c_1);
  and and_2 (and_2_out, c_3, not_3_out, c_0);
  not not_4 (not_4_out, c_3);
  and and_3 (and_3_out, not_4_out, c_1, c_0);
  not not_5 (not_5_out, c_3);
  not not_6 (not_6_out, c_1);
  and and_4 (and_4_out, not_5_out, not_6_out, not_7_out);
  not not_7 (not_7_out, c_0);
  not not_8 (not_8_out, c_2);
  and and_5 (and_5_out, not_8_out, not_9_out);
  not not_9 (not_9_out, c_0);
  or or_1 (s_1, and_1_out, and_2_out, and_3_out, and_4_out, and_5_out);
endmodule

module segment_2 (
  input  c_3,
  input  c_2,
  input  c_1,
  input  c_0,
  output s_2
);

  wire and_1_out, and_2_out, and_3_out, and_4_out, and_5_out, not_1_out, not_2_out, not_3_out, not_4_out,
       not_5_out, not_6_out;

  not not_1 (not_1_out, c_2);
  not not_2 (not_2_out, c_3);
  not not_3 (not_3_out, c_3);
  not not_4 (not_4_out, c_1);
  not not_5 (not_5_out, c_3);
  not not_6 (not_6_out, c_1);
  and and_1 (and_1_out, c_3, not_1_out);
  and and_2 (and_2_out, not_2_out, c_2);
  and and_3 (and_3_out, not_3_out, not_4_out);
  and and_4 (and_4_out, not_5_out, c_0);
  and and_5 (and_5_out, not_6_out, c_0);
  or or_1 (s_2, and_1_out, and_2_out, and_3_out, and_4_out, and_5_out);
endmodule

module segment_3 (
  input  c_3,
  input  c_2,
  input  c_1,
  input  c_0,
  output s_3
);

  wire and_1_out, and_2_out, and_3_out, and_4_out, and_5_out, not_1_out, not_2_out, not_3_out, not_4_out,
       not_5_out, not_6_out, not_7_out;

  and and_1 (and_1_out, c_3, not_1_out);
  not not_1 (not_1_out, c_1);
  not not_2 (not_2_out, c_3);
  not not_3 (not_3_out, c_2);
  and and_2 (and_2_out, not_2_out, not_3_out, not_4_out);
  not not_4 (not_4_out, c_0);
  and and_3 (and_3_out, c_2, c_1, not_5_out);
  not not_5 (not_5_out, c_0);
  not not_6 (not_6_out, c_1);
  and and_4 (and_4_out, c_2, not_6_out, c_0);
  not not_7 (not_7_out, c_2);
  and and_5 (and_5_out, not_7_out, c_1, c_0);
  or or_1 (s_3, and_1_out, and_2_out, and_3_out, and_4_out, and_5_out);
endmodule

module segment_4 (
  input  c_3,
  input  c_2,
  input  c_1,
  input  c_0,
  output s_4
);

  wire and_1_out, and_2_out, and_3_out, and_4_out, not_1_out, not_2_out, not_3_out;

  and and_1 (and_1_out, c_3, c_2);
  and and_2 (and_2_out, c_3, c_1);
  not not_1 (not_1_out, c_2);
  and and_3 (and_3_out, not_1_out, not_2_out);
  not not_2 (not_2_out, c_0);
  and and_4 (and_4_out, c_1, not_3_out);
  not not_3 (not_3_out, c_0);
  or or_1 (s_4, and_1_out, and_2_out, and_3_out, and_4_out);
endmodule

module segment_5 (
  input  c_3,
  input  c_2,
  input  c_1,
  input  c_0,
  output s_5
);

  wire and_1_out, and_2_out, and_3_out, and_4_out, and_5_out, not_1_out, not_2_out, not_3_out, not_4_out,
       not_5_out, not_6_out;

  not not_1 (not_1_out, c_2);
  not not_2 (not_2_out, c_3);
  not not_3 (not_3_out, c_1);
  not not_4 (not_4_out, c_0);
  not not_5 (not_5_out, c_1);
  not not_6 (not_6_out, c_0);
  and and_1 (and_1_out, c_3, not_1_out);
  and and_2 (and_2_out, not_2_out, c_2, not_3_out);
  and and_3 (and_3_out, c_3, c_1);
  and and_4 (and_4_out, c_2, not_4_out);
  and and_5 (and_5_out, not_5_out, not_6_out);
  or or_1 (s_5, and_1_out, and_2_out, and_3_out, and_4_out, and_5_out);
endmodule

module segment_6 (
  input  c_3,
  input  c_2,
  input  c_1,
  input  c_0,
  output s_6
);

  wire and_1_out, and_2_out, and_3_out, and_4_out, and_5_out, not_1_out, not_2_out, not_3_out, not_4_out,
       not_5_out;

  not not_1 (not_1_out, c_2);
  not not_2 (not_2_out, c_3);
  not not_3 (not_3_out, c_1);
  not not_4 (not_4_out, c_2);
  not not_5 (not_5_out, c_0);
  and and_1 (and_1_out, c_3, not_1_out);
  and and_2 (and_2_out, not_2_out, c_2, not_3_out);
  and and_3 (and_3_out, not_4_out, c_1);
  and and_4 (and_4_out, c_3, c_0);
  and and_5 (and_5_out, c_1, not_5_out);
  or or_1 (s_6, and_1_out, and_2_out, and_3_out, and_4_out, and_5_out);
endmodule

module decoder_7_segment (
  input  c_3,
  input  c_2,
  input  c_1,
  input  c_0,
  output out_5,
  output out_6,
  output out_7,
  output out_8,
  output out_9,
  output out_10,
  output out_11
);

  segment_0 segment_0_1 (.c_3(c_3), .c_2(c_2), .c_1(c_1), .c_0(c_0), .s_0(out_5));
  segment_1 segment_1_1 (.c_3(c_3), .c_2(c_2), .c_1(c_1), .c_0(c_0), .s_1(out_6));
  segment_2 segment_2_1 (.c_3(c_3), .c_2(c_2), .c_1(c_1), .c_0(c_0), .s_2(out_7));
  segment_3 segment_3_1 (.c_3(c_3), .c_2(c_2), .c_1(c_1), .c_0(c_0), .s_3(out_8));
  segment_4 segment_4_1 (.c_3(c_3), .c_2(c_2), .c_1(c_1), .c_0(c_0), .s_4(out_9));
  segment_5 segment_5_1 (.c_3(c_3), .c_2(c_2), .c_1(c_1), .c_0(c_0), .s_5(out_10));
  segment_6 segment_6_1 (.c_3(c_3), .c_2(c_2), .c_1(c_1), .c_0(c_0), .s_6(out_11));
endmodule
