// Logisim project Part 2 q3 mux4to1.circ as structural Verilog: 3 circuits, main circuit main
module main (
  input  SW_0,
  input  SW_1,
  input  SW_9,
  output LEDR_9
);

  mux2to1 u (.x(SW_0), .y(SW_1), .s(SW_9), .m(LEDR_9));
endmodule

module mux2to1 (
  input  x,
  input  y,
  input  s,
  output m
);

  Multiplexer #(.enable("false")) multiplexer_1 (.in0(x), .in1(y), .out(m), .sel(s));
endmodule

module mux4to1 (
  input  u,
  input  v,
  input  w,
  input  x,
  input  s_1,
  input  s_0,
  output m
);

  wire mux2to1_0_m, mux2to1_1_m;

  mux2to1 mux2to1_0 (.x(u), .y(w), .s(s_1), .m(mux2to1_0_m));
  mux2to1 mux2to1_1 (.x(v), .y(x), .s(s_1), .m(mux2to1_1_m));
  mux2to1 mux2to1_2 (.x(mux2to1_0_m), .y(mux2to1_1_m), .s(s_0), .m(m));
endmodule
