// Logisim project mux.circ as structural Verilog: 4 circuits, main circuit main
module main (
  input  SW_0,
  input  SW_1,
  input  SW_9,
  output LEDR_9
);

  mux2to1 u (.x(SW_0), .y(SW_1), .s(SW_9), .m(LEDR_9));
endmodule

module mux2to1 (
  input  x,
  input  y,
  input  s,
  output m
);

  Multiplexer #(.enable("false")) multiplexer_1 (.in0(x), .in1(y), .out(m), .sel(s));
endmodule

module mux4to1 (
  input  u,
  input  v,
  input  w,
  input  x,
  input  s_1,
  input  s_0,
  output m
);

  wire mux2to1_1_m, mux2to1_3_m;

  mux2to1 mux2to1_1 (.x(u), .y(w), .s(s_1), .m(mux2to1_1_m));
  mux2to1 mux2to1_3 (.x(v), .y(x), .s(s_1), .m(mux2to1_3_m));
  mux2to1 mux2to1_2 (.x(mux2to1_1_m), .y(mux2to1_3_m), .s(s_0), .m(m));
endmodule

module mux4to1_de1soc (
  input  SW_0,
  input  SW_1,
  input  SW_2,
  input  SW_3,
  input  SW_9,
  input  SW_8,
  output LEDR_0
);

  wire mux2to1_1_m, mux2to1_2_m;

  mux2to1 mux2to1_1 (.x(SW_0), .y(SW_2), .s(SW_9), .m(mux2to1_1_m));
  mux2to1 mux2to1_2 (.x(SW_1), .y(SW_3), .s(SW_9), .m(mux2to1_2_m));
  mux2to1 mux2to1_3 (.x(mux2to1_1_m), .y(mux2to1_2_m), .s(SW_8), .m(LEDR_0));
endmodule
