// Logisim project p3.circ as structural Verilog
module shifter_bit (
  input  sb_in,
  input  load_val,
  input  shift,
  input  load_n,
  input  clk,
  input  reset,
  output sb_out
);

  wire mux2to1_1_m, mux2to1_2_m;

  mux2to1 mux2to1_1 (.x(sb_out), .y(sb_in), .s(shift), .m(mux2to1_1_m));
  mux2to1 mux2to1_2 (.x(load_val), .y(mux2to1_1_m), .s(load_n), .m(mux2to1_2_m));
  D_Flip_Flop d_ff_1 (.D(mux2to1_2_m), .clk(clk), .Q(sb_out), .reset(reset));  // open: Qn, preset
endmodule

module mux2to1 (
  input  x,
  input  y,
  input  s,
  output m
);

  Multiplexer #(.enable("false")) multiplexer_1 (.in0(x), .in1(y), .out(m), .sel(s));
endmodule

module mux4to1 (
  input  u,
  input  v,
  input  w,
  input  x,
  input  s_1,
  input  s_0,
  output m
);

  wire mux2to1_0_m, mux2to1_1_m;

  mux2to1 mux2to1_0 (.x(u), .y(w), .s(s_1), .m(mux2to1_0_m));
  mux2to1 mux2to1_1 (.x(v), .y(x), .s(s_1), .m(mux2to1_1_m));
  mux2to1 mux2to1_2 (.x(mux2to1_0_m), .y(mux2to1_1_m), .s(s_0), .m(m));
endmodule

module shift_register (
  input  ASR,
  input  [7:0] LoadVal,
  input  ShiftRight,
  input  load_n,
  input  in_5,
  input  in_6,
  input  in_7,
  input  [3:0] in_8,
  output [7:0] Q,
  output [3:0] out_10
);

  wire and_1_out, button_1_out, clock_out, reset_out;

  Button clock (.out(clock_out));
  Button reset (.out(reset_out));
  and and_1 (and_1_out, ASR, LoadVal[7]);
  Button button_1 (.out(button_1_out));
  // Shift_Register #(.length(4)) shift_register_1: pin names not known; wires that end beside it: in_5, in_6, in_7, button_1_out
  shifter_bit shifter_bit_1 (
    .sb_in(and_1_out), .load_val(LoadVal[7]), .shift(ShiftRight), .load_n(load_n), .clk(clock_out),
    .reset(reset_out), .sb_out(Q[7]));
  shifter_bit shifter_bit_2 (
    .sb_in(Q[7]), .load_val(LoadVal[6]), .shift(ShiftRight), .load_n(load_n), .clk(clock_out),
    .reset(reset_out), .sb_out(Q[6]));
  shifter_bit shifter_bit_3 (
    .sb_in(Q[6]), .load_val(LoadVal[5]), .shift(ShiftRight), .load_n(load_n), .clk(clock_out),
    .reset(reset_out), .sb_out(Q[5]));
  shifter_bit shifter_bit_4 (
    .sb_in(Q[5]), .load_val(LoadVal[4]), .shift(ShiftRight), .load_n(load_n), .clk(clock_out),
    .reset(reset_out), .sb_out(Q[4]));
  shifter_bit shifter_bit_5 (
    .sb_in(Q[4]), .load_val(LoadVal[3]), .shift(ShiftRight), .load_n(load_n), .clk(clock_out),
    .reset(reset_out), .sb_out(Q[3]));
  shifter_bit shifter_bit_6 (
    .sb_in(Q[3]), .load_val(LoadVal[2]), .shift(ShiftRight), .load_n(load_n), .clk(clock_out),
    .reset(reset_out), .sb_out(Q[2]));
  shifter_bit shifter_bit_7 (
    .sb_in(Q[2]), .load_val(LoadVal[1]), .shift(ShiftRight), .load_n(load_n), .clk(clock_out),
    .reset(reset_out), .sb_out(Q[1]));
  shifter_bit shifter_bit_8 (
    .sb_in(Q[1]), .load_val(LoadVal[0]), .shift(ShiftRight), .load_n(load_n), .clk(clock_out),
    .reset(reset_out), .sb_out(Q[0]));
endmodule
